# Fritzing sketch curcite block (saved by Fritzing 0.9.5d)
breadboards: 9

parts:
  IC3 = Atmega8 [package=dil28-3-simon]
  L298N1 = L298N DC motor driver
  M1 = DC Motor
  XTAL1 = Crystal [frequency="16 Mhz" package=THT]
  VCC1 = Battery block 9V
  C1 = Capacitor [package=cap-pth-small2]
  C2 = Capacitor [package=cap-pth-small2]
  U4 = Voltage Regulator - 5V [package="DPak [SMD]"]
  S2 = Pushbutton [package=THT]
  R6 = Resistor [tolerance=±5% resistance=220 package=THT]
  R4 = Resistor [tolerance=±5% resistance=220 package="2010 [SMD]"]
  R2 = Resistor [tolerance=±5% resistance=220 package="2010 [SMD]"]
  C5 = Capacitor [package=cap-pth-small2]
  R3 = Resistor [tolerance=±5% resistance=220 package="2010 [SMD]"]
  Part2 = NRF24L01+ Breakout Board
  C6 = Electrolytic Capacitor [capacitance=10μF package="0605 [SMD, electrolytic]"]
  U5 = Voltage Regulator [package=to220-adj]
  C4 = Electrolytic Capacitor [capacitance=10μF package="0605 [SMD, electrolytic]"]
  SG1 = Buzzer 12mm [package=buzzer-12mm-ns-kit]
  Jetson_Nano1 = Jetson Nano
  J1 = Basic Servo
  C3 = Electrolytic Capacitor [capacitance=10μF package="0605 [SMD, electrolytic]"]
  VCC2 = Battery block 9V
  U2 = RFID RC522 SIP - 8 pins [chip_label="RFID RC522" package="SIP (Single Inline) [THT]"]
  U1 = RFID RC522 SIP - 8 pins [chip_label="RFID RC522" package="SIP (Single Inline) [THT]"]
  U3 = RFID RC522 SIP - 8 pins [chip_label="RFID RC522" package="SIP (Single Inline) [THT]"]
  J2 = Basic Servo
  HC-SR04_Sensor_1 = HC-SR04 Ultrasonic Distance Sensor  # not connected
  R1 = Resistor [tolerance=±5% resistance=220 package="2010 [SMD]"]
  Part1 = NRF24L01+ Breakout Board

nets:
  N1: IC3.PC6(_RESET), S2.leg0, R6.Pin_1
  N2: IC3.PD2(INT0), Part2.IRQ
  N3: IC3.PD3(INT1), L298N1.ENA
  N4: IC3.VCC, U4.output_voltage, R6.Pin_0
  GND: IC3.GND, L298N1.GND, VCC1.-, C1.2, C2.1, U4.GND, S2.leg1, R4.Pin_0, C5.1, C6.-
  N5: IC3.PB6(XTAL1_TOSC1), XTAL1.pin_0, C2.2
  N6: IC3.PB7(XTAL2_TOSC2), XTAL1.pin_1, C1.1
  N7: IC3.PB1(OC1A), Part2.CS
  N8: IC3.PB2(SS_OC1B), Part2.CE
  N9: IC3.PB3(MOSI_OC2), Part2.MOSI
  N10: IC3.PB4(MISO), Part2.MISO
  N11: IC3.PB5(SCK), Part2.SCK
  N12: IC3.PC0(ADC0), L298N1.IN2
  N13: IC3.PC1(ADC1), L298N1.5V, L298N1.IN1
  N14: L298N1.OUT1, M1.pin_2
  N15: L298N1.OUT2, M1.pin_1
  N16: L298N1.12V, VCC1.+, U4.input_voltage, U5.OUT, C4.+
  N17: R4.Pin_1, R2.Pin_0
  N18: R2.Pin_1, R3.Pin_0, Part2.GND, U5.ADJ, C4.-
  N19: C5.2, R3.Pin_1, Part2.VCC, C6.+, U5.IN
  N20: SG1.1, Jetson_Nano1.GPIO15
  GND_2: SG1.2, Jetson_Nano1.GPIO19, J1.gnd, C3.-, VCC2.-, U1.GND, J2.gnd, Part1.GND
  3V3: Jetson_Nano1.3v3, Jetson_Nano1.3V3, U3.NSS, R1.Pin_0, Part1.IRQ
  N21: Jetson_Nano1.GND, U2.MISO, U3.MISO, J2.pulse, Part1.CS
  N22: Jetson_Nano1.GPIO22, U2.NSS
  N23: Jetson_Nano1.GPIO10, U1.MISO, Part1.MISO
  N24: Jetson_Nano1.GPIO11, U1.NSS
  N25: Jetson_Nano1.GPIO5, U2.RST, U1.RST, U3.RST
  VCC: Jetson_Nano1.GPIO21, C3.+, U1.VCC, R1.Pin_1, Part1.VCC
  N26: Jetson_Nano1.ID_SC, U1.SCK, Part1.SCK
  N27: Jetson_Nano1.GPIO25, U2.MOSI, U3.MOSI
  N28: Jetson_Nano1.GPIO24, U2.SCK, U3.SCK
  N29: Jetson_Nano1.GPIO14, J1.pulse
  N30: Jetson_Nano1.5V, U1.MOSI, Part1.MOSI
  VCC_2: J1.vcc, VCC2.+, J2.vcc
  GND_3: U2.GND, U3.GND
  VCC_3: U2.VCC, U3.VCC

notes:
  L298N
  PC1 IN1 green
  PC0 IN2 orange
  PD3 ENA white
  out1 red
  out2 black
  L7805
  input ground 5v

custom parts:
  Atmega8: MICROCONTROLLER 8 Kbytes FLASH 1 kbytes SRAM 512 bytes EEPROM USART 4-channel 10 bit ADC 2-channel 8 bit ADC
  L298N DC motor driver: 2x DC motor driver with 78M05 positive voltage regulator (7..35 V) L298N: max 46 V, 2 A Set 5 V Enable jumper to enable 5 V regultor (needed for the L298N) and +5 V output at screw terminal or supply external +5 V at screw terminal Set ENA and/or ENB to +5 V to enable motor permanently or supply ENA and/or ENB with PWM signal IN1 and IN2 set rotation directory for motor A (OUT1/OUT2) IN2 and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
  RFID RC522 SIP - 8 pins: A SIP stand-in part for RFID RC522 . With 8 pins on a 300 mil single inline package (SIP) footprint.
